# Fritzing sketch Line follower wiring schematic (saved by Fritzing 0.9.6b)
breadboards: 1

parts:
  M1 = gear-motor [part_number="MOTOR LEFT"]
  M2 = gear-motor [part_number="MOTOR RIGHT"]
  VCC1 = 4 x AAA Battery Mount
  HC-SR04_Sensor_1 = HC-SR04 Ultrasonic Distance Sensor
  U2 = QTR-3A Reflectance Sensor Array [package=THT]
  A1 = 1x18650 battery shield [package=THT]
  SW1 = Slide_Switch_new
  Part2 = Arduino Mega 2560 (Rev3)
  LCD2 = LCD screen
  LCM1602_IIC2 = LCM1602 IIC [part_number="LCM1602 IIC" chip_label="LCM1602 IIC" package="DIP (Dual Inline) [THT]"]
  U3 = L9110 H-bridge module [part_number="L9110 H-bridge"]
  S1 = Momentary Switch [package=ksa_sealed_tac_switch]
  R1 = Resistor [tolerance=±5% resistance=10k package="1206 [SMD]"]
  U4 = ESP32-38PinWide [part_number=ESP32-38PinWide]
  LED1 = RGB LED (com. anode, rbg) [package="5 mm [THT]"]  # not connected
  R2 = Resistor [tolerance=±5% resistance=10k package="1206 [SMD]"]  # not connected

nets:
  N1: M1.pin_1, U3.MOTOR_B-B
  N2: M1.pin_2, U3.MOTOR_B-A
  N3: M2.pin_1, U3.MOTOR_A-A
  N4: M2.pin_2, U3.MOTOR_A-B
  N5: VCC1.+, U3.VCC
  VCC: HC-SR04_Sensor_1.VCC, A1.pin_7, Part2.5V, S1.3
  N6: HC-SR04_Sensor_1.TRIG, Part2.D22
  N7: HC-SR04_Sensor_1.ECHO, Part2.D23
  GND: HC-SR04_Sensor_1.GND, Part2.GND, U3.GND, R1.Pin_0
  N8: U2.GND, Part2.A2
  N9: U2.VCC, Part2.A1
  N10: U2.1, Part2.A0
  N11: A1.pin_8, SW1.pin_1
  N12: Part2.A4, LCM1602_IIC2.SDA
  N13: Part2.A5, LCM1602_IIC2.SCL
  N14: Part2.D13_PWM, S1.1, R1.Pin_1
  N15: Part2.D12_PWM, U4.GPIO17
  N16: Part2.D11_PWM, U4.GPIO16
  N17: Part2.D3_PWM, U3.A-IB
  N18: Part2.D4_PWM, U3.A-IA
  N19: Part2.D6_PWM, U3.B-IB
  N20: Part2.D7_PWM, U3.B-IA
  VSS: LCD2.VSS, LCM1602_IIC2.VSS
  VDD: LCD2.VDD, LCM1602_IIC2.VDD
  N21: LCD2.V0, LCM1602_IIC2.V0
  N22: LCD2.RS, LCM1602_IIC2.RS
  N23: LCD2.R/W, LCM1602_IIC2.RW
  N24: LCD2.E, LCM1602_IIC2.E
  N25: LCD2.DB0, LCM1602_IIC2.D0
  N26: LCD2.DB1, LCM1602_IIC2.D1
  N27: LCD2.DB2, LCM1602_IIC2.D2
  N28: LCD2.DB3, LCM1602_IIC2.D3
  N29: LCD2.DB4, LCM1602_IIC2.D4
  N30: LCD2.DB5, LCM1602_IIC2.D5
  N31: LCD2.DB6, LCM1602_IIC2.D6
  N32: LCD2.DB7, LCM1602_IIC2.D7
  N33: LCD2.LED+, LCM1602_IIC2.A
  N34: LCD2.LED-, LCM1602_IIC2.K
  N35: LCM1602_IIC2.LED_A, LCM1602_IIC2.LED_B

custom parts:
  1x18650 battery shield: 1x18650 Lithium Battery Shield V3 CC CV Type-C Micro USB Mobile Power Bank DIY Module 5V 3A 3V 1A for iPhone Samsung Xiaomi.
  Slide_Switch_new: the New two pin slide switch
  LCM1602 IIC: I2C-Module to use a 1602 or 2004 LCD on with the wire.h libory Serial LCD Modul
  ESP32-38PinWide: Generic 38-Pin ESP32 with wide format (only access to one side of pins on a breadboard) based on Stephen Lilley's HiLetgo ESP-WROOM-32 ESP32 ESP-32S Development Board.
